// Logisim project LOBOPT2.circ as structural Verilog: 5 circuits, main circuit main
module main (
  input  in_1,
  output [7:0] out_2,
  output [7:0] out_3
);

  wire AluSre, CLC, MemRead, MemToReg, MemWrite, rammemory_1_p6, Regwrite, ula_1_pcplus;
  wire [3:0] Mux, OPCd;
  wire [7:0] adder_1_out, bit_extender_1_out, multiplexer_1_out, multiplexer_3_out, R0, rammemory_1_p8,
       register_1_q, registerbank_1_saida, registerbank_1_saida2;

  Clock clock_1 (.out(CLC));
  Register #(.trigger("falling")) register_1 (
    .D(multiplexer_1_out), .en(1'b1), .clk(CLC), .Q(register_1_q), .clr(in_1));
  ROM rom_1 (.addr(register_1_q), .data({OPCd, Mux}));
  Adder adder_1 (.a(8'h1), .b(register_1_q), .out(adder_1_out));  // open: cin, cout
  Multiplexer #(.width(8), .enable("false")) multiplexer_1 (
    .in0(adder_1_out), .in1(out_3), .out(multiplexer_1_out), .sel(ula_1_pcplus));
  registerBank registerbank_1 (
    .ReadRegs1(Mux[1:0]), .ReadRegs2(Mux[3:2]), .inserieRegs(Regwrite), .WriteRegs(Mux[1:0]),
    .WriteData(multiplexer_3_out), .Clock(CLC), .Rest(in_1), .Saida(registerbank_1_saida),
    .Saida2(registerbank_1_saida2), .REGs0(R0));
  ControleDaULaprr controledaulaprr_1 (
    .A(OPCd[3]), .B(OPCd[2]), .C(OPCd[1]), .D(OPCd[0]), .AluSre(AluSre), .MemToReg(MemToReg),
    .MemWrite(MemWrite), .Regwrite(Regwrite), .MemRead(MemRead));
  assign bit_extender_1_out = {{4{Mux[3]}}, Mux};  // Bit_Extender bit_extender_1
  Multiplexer #(.width(8), .enable("false")) multiplexer_2 (
    .in0(registerbank_1_saida2), .in1(bit_extender_1_out), .out(out_2), .sel(AluSre));
  ULA ula_1 (
    .A(registerbank_1_saida), .B(out_2), .Shamt(out_2[2:0]), .Regs0(R0), .PC({OPCd, Mux}), .Funtion(OPCd),
    .Result(out_3), .PCplus(ula_1_pcplus));
  // RamMemory rammemory_1: pin names not known; wires that end beside it: MemWrite, out_3, registerbank_1_saida2, CLC, MemRead, rammemory_1_p6, rammemory_1_p6, rammemory_1_p8
  Multiplexer #(.width(8), .enable("false")) multiplexer_3 (
    .in0(out_3), .in1(rammemory_1_p8), .out(multiplexer_3_out), .sel(MemToReg));

  // Other names for the same wires on the sheet: PC[7:0] = {OPCd, Mux}; RST = in_1

  // Notes on the sheet:
  //   contents of rom_1 (hex, n*v repeats v):
  //   70 91 aa 41 47 96 9c 51 51 94 9e 98
endmodule

module registerBank (
  input  [1:0] ReadRegs1,
  input  [1:0] ReadRegs2,
  input  inserieRegs,
  input  [1:0] WriteRegs,
  input  [7:0] WriteData,
  input  Clock,
  input  Rest,
  output [7:0] Saida,
  output [7:0] Saida2,
  output [7:0] REGs0
);

  wire demultiplexer_1_out0, demultiplexer_1_out1, demultiplexer_1_out2, demultiplexer_1_out3;
  wire [7:0] demultiplexer_2_out0, demultiplexer_2_out1, demultiplexer_2_out2, demultiplexer_2_out3, regs1,
       regs2, regs3;

  Demultiplexer #(.select(2), .enable("false")) demultiplexer_1 (
    .out0(demultiplexer_1_out0), .out1(demultiplexer_1_out1), .out2(demultiplexer_1_out2),
    .out3(demultiplexer_1_out3), .in(inserieRegs), .sel(WriteRegs));
  Demultiplexer #(.select(2), .width(8), .enable("false")) demultiplexer_2 (
    .out0(demultiplexer_2_out0), .out1(demultiplexer_2_out1), .out2(demultiplexer_2_out2),
    .out3(demultiplexer_2_out3), .in(WriteData), .sel(WriteRegs));
  Register regs (.D(demultiplexer_2_out0), .en(demultiplexer_1_out0), .clk(Clock), .Q(REGs0), .clr(Rest));
  Register u_regs1 (.D(demultiplexer_2_out1), .en(demultiplexer_1_out1), .clk(Clock), .Q(regs1), .clr(Rest));
  Register u_regs2 (.D(demultiplexer_2_out2), .en(demultiplexer_1_out2), .clk(Clock), .Q(regs2), .clr(Rest));
  Register u_regs3 (.D(demultiplexer_2_out3), .en(demultiplexer_1_out3), .clk(Clock), .Q(regs3), .clr(Rest));
  Multiplexer #(.select(2), .width(8), .enable("false")) multiplexer_1 (
    .in0(REGs0), .in1(regs1), .in2(regs2), .in3(regs3), .out(Saida), .sel(ReadRegs1));
  Multiplexer #(.select(2), .width(8), .enable("false")) multiplexer_2 (
    .in0(regs3), .in1(regs2), .in2(regs1), .in3(REGs0), .out(Saida2), .sel(ReadRegs2));

  // Other names for the same wires on the sheet: regs[7:0] = REGs0; Seletor[1:0] = ReadRegs1;
  //   Seletor1[1:0] = ReadRegs2
endmodule

module ULA (
  input  [7:0] A,
  input  [7:0] B,
  input  [2:0] Shamt,
  input  [7:0] Regs0,
  input  [7:0] PC,
  input  [3:0] Funtion,
  output [7:0] Result,
  output PCplus
);

  wire C1E, C2E;
  wire [7:0] A1, A2, A3, A4, A5, A6, A7, A8, A9, A10, A11, A12, A13, A14, A15, A16, adder_1_out, B1, B2, B3,
       B4, B5, B6, B7, B8, B9, B10, B11, B12, B13, B14, B15, B16, bit_extender_1_out, bit_extender_2_out, C1,
       C2, C4, C8, C9, C10, C11, C12, C13, C14, C15, C16;

  Multiplexer #(.width(8), .enable("false")) multiplexer_1 (.in1(B1), .out(C1), .sel(C1E));  // open: in0
  Comparator comparator_1 (.a(A1), .b({8{1'b0}}), .eq(C1E));  // open: gt, lt
  Adder adder_1 (.a(B2), .b(PC), .out(adder_1_out));  // open: cin, cout
  Comparator comparator_2 (.a(Regs0), .b({8{1'b0}}), .eq(C2E));  // open: gt, lt
  Adder adder_2 (.a(B4), .b(Regs0), .out(C4));  // open: cin, cout
  assign bit_extender_1_out = {{4{Regs0[7]}}, Regs0[7:4]};  // Bit_Extender bit_extender_1
  Multiplexer #(.width(8), .enable("false")) multiplexer_2 (.in1(adder_1_out), .out(C2), .sel(C2E));  // open: in0
  Adder adder_3 (.a(bit_extender_1_out), .b(B8), .out(C8));  // open: cin, cout
  Demultiplexer #(.select(4), .width(8), .enable("false")) demultiplexer_1 (
    .out0(A1), .out1(A2), .out2(A3), .out3(A4), .out4(A5), .out5(A6), .out6(A7), .out7(A8), .out8(A9),
    .out9(A10), .out10(A11), .out11(A12), .out12(A13), .out13(A14), .out14(A15), .out15(A16), .in(A),
    .sel(Funtion));
  Demultiplexer #(.select(4), .width(8), .enable("false")) demultiplexer_2 (
    .out0(B1), .out1(B2), .out2(B3), .out3(B4), .out4(B5), .out5(B6), .out6(B7), .out7(B8), .out8(B9),
    .out9(B10), .out10(B11), .out11(B12), .out12(B13), .out13(B14), .out14(B15), .out15(B16), .in(B),
    .sel(Funtion));
  Multiplexer #(.select(4), .width(8), .enable("false")) multiplexer_3 (
    .in0(C1), .in1(C2), .in2(B3), .in3(C4), .in4(B5), .in5(B6), .in6(B7), .in7(C8), .in8(C9), .in9(C10),
    .in10(C11), .in11(C12), .in12(C13), .in13(C14), .in14(C15), .in15(C16), .out(Result), .sel(Funtion));
  Multiplexer #(.select(4), .enable("false")) multiplexer_4 (
    .in0(C1E), .in1(C2E), .in2(1'b1), .in3(1'b1), .in4(1'b0), .in5(1'b0), .in6(1'b0), .in7(1'b0), .in8(1'b0),
    .in9(1'b0), .in10(1'b0), .in11(1'b0), .in12(1'b0), .in13(1'b0), .in14(1'b0), .in15(1'b0), .out(PCplus),
    .sel(Funtion));
  assign bit_extender_2_out = {{4{Regs0[3]}}, Regs0[3:0]};  // Bit_Extender bit_extender_2
  Adder adder_4 (.a(A10), .b(B10), .out(C10));  // open: cin, cout
  Subtractor subtractor_1 (.a(A11), .b(B11), .out(C11));  // open: bin, bout
  assign C14 = ~A14;  // NOT_Gate not_1, 8 bits wide
  Shifter shifter_1 (.in(A15), .\dist (Shamt), .out(C15));
  Shifter #(.shift("lr")) shifter_2 (.in(A16), .\dist (Shamt), .out(C16));
  Adder adder_5 (.a(B9), .b(bit_extender_2_out), .out(C9));  // open: cin, cout
  assign C12 = A12 & B12;  // AND_Gate and_1, 8 bits wide
  assign C13 = A13 | B13;  // OR_Gate or_1, 8 bits wide

  // Other names for the same wires on the sheet: C3[7:0] = B3; C5[7:0] = B5; C6[7:0] = B6; C7[7:0] = B7;
  //   DD[3:0] = Funtion; R0[7:0] = Regs0; R4_7[3:0] = Regs0[3:0]; R0_3[3:0] = Regs0[7:4]

  // Notes on the sheet:
  //   1=branch on zero Register
  //   2=Branch on zero immediate
  //   3=Jump register
  //   4=jump immediate
  //   5=Load
  //   6=Store
  //   7=Move Register
  //   8= move High
  //   9=Move Low
  //   10=Add
  //   11=Sub
  //   12=And
  //   13=Or
  //   14=Not
  //   15=Shift left Register
  //   16=Shift Right Register
endmodule

module RamMemory (
  input  Leitura,
  input  Escrita,
  input  [7:0] Endereco,
  input  [7:0] Entrada,
  input  clock,
  output [7:0] Saida
);

  wire [7:0] ram_1_data;

  RAM #(.trigger("falling")) ram_1 (.addr(Endereco), .we(Escrita), .oe(Leitura), .clk(clock), .data(ram_1_data));
  Demultiplexer #(.width(8), .enable("false")) demultiplexer_1 (
    .out1(Saida), .in(ram_1_data), .sel(Leitura));  // open: out0
  Multiplexer #(.width(8), .enable("false")) multiplexer_1 (
    .in1(Entrada), .out(ram_1_data), .sel(Escrita));  // open: in0

  // Other names for the same wires on the sheet: MemRead = Leitura; MemWrite = Escrita
endmodule

module ControleDaULaprr (
  input  A,
  input  B,
  input  C,
  input  D,
  output AluSre,
  output MemToReg,
  output MemWrite,
  output Regwrite,
  output MemRead
);

  wire and_1_out, and_4_out, and_5_out, and_6_out, and_7_out, not_1_out, not_2_out, not_3_out, not_4_out,
       not_5_out, not_6_out, not_7_out, not_8_out, not_9_out, not_10_out, not_11_out, not_12_out, not_13_out,
       not_14_out, not_15_out, not_16_out;

  not not_1 (not_1_out, A);
  not not_2 (not_2_out, B);
  not not_3 (not_3_out, A);
  not not_4 (not_4_out, B);
  not not_5 (not_5_out, A);
  not not_6 (not_6_out, B);
  not not_7 (not_7_out, C);
  not not_8 (not_8_out, D);
  not not_9 (not_9_out, A);
  not not_10 (not_10_out, B);
  and and_1 (and_1_out, not_10_out, not_11_out, not_12_out);
  not not_11 (not_11_out, C);
  not not_12 (not_12_out, D);
  not not_13 (not_13_out, A);
  and and_2 (MemWrite, not_13_out, B, not_14_out);
  not not_14 (not_14_out, D);
  not not_15 (not_15_out, D);
  or or_1 (Regwrite, not_15_out, C, A);
  not not_16 (not_16_out, A);
  and and_3 (MemRead, not_16_out, B, D);
  and and_4 (and_4_out, not_1_out, not_2_out, D);
  and and_5 (and_5_out, not_3_out, not_4_out, C);
  and and_6 (and_6_out, not_5_out, C, D);
  and and_7 (and_7_out, A, not_6_out, not_7_out, not_8_out);
  or or_2 (MemToReg, not_9_out, and_1_out);
  or or_3 (AluSre, and_4_out, and_5_out, and_6_out, and_7_out);
endmodule
